# Fritzing sketch TeeterTotter-WiringFritzing (saved by Fritzing 0.9.10b)

parts:
  APA102_LED_Strip1 = APA102 LED Strip [part_number=14015]
  Part1 = Arduino Uno (Rev3)
  J1 = Power Jack [package=power_jack_slot]
  U1 = POT [knob_status=50% power=0.5W package=pot_alpha_rv16af-20]
  APA102_LED_Strip2 = APA102 LED Strip [part_number=14015]

nets:
  GND: APA102_LED_Strip1.GND, Part1.GND, J1.GND, U1.E, APA102_LED_Strip2.GND
  N1: APA102_LED_Strip1.CI, Part1.D11_PWM/MOSI, APA102_LED_Strip2.CI
  N2: APA102_LED_Strip1.DI, Part1.D13/SCK, APA102_LED_Strip2.DI
  +5V: APA102_LED_Strip1.+5V, Part1.5V, J1.PWR, U1.A, APA102_LED_Strip2.+5V
  N3: Part1.A0, U1.S

custom parts:
  APA102 LED Strip: APA102 LED strip, white, 60 LEDs/m
